# Fritzing sketch Microdex1 (saved by Fritzing 0.9.9b)
stripboards: 1

parts:
  RE1 = KY-040 Rotary encoder [package="Breakout board"]
  J2 = male pin header, 6 pins [form="♂ (male)"]
  RE2 = KY-040 Rotary encoder [package="Breakout board"]
  U1 = MIDI_CONN_FEMALE_SUPPORT [package=din_5_female_support]
  D1 = Rectifier Diode [part_number=1N4001 package="300 mil [THT]"]
  C3 = Ceramic Capacitor [capacitance=100nF voltage=35V package="100 mil [THT, multilayer]"]
  C5 = Electrolytic Capacitor [capacitance=1µF voltage=35V package="100 mil [THT, electrolytic]"]
  U3 = MIDI_CONN_FEMALE_SUPPORT [package=din_5_female_support]
  Teensy1 = Teensy 3.6 (Basic)
  J5 = male pin header, 4 pins [form="♂ (male)"]
  C7 = Electrolytic Capacitor [capacitance=1µF voltage=35V package="100 mil [THT, electrolytic]"]
  C8 = Ceramic Capacitor [capacitance=100nF voltage=35V package="100 mil [THT, multilayer]"]
  J7 = male pin header, 3 pins [form="♂ (male)"]
  J8 = male pin header, 3 pins [form="♂ (male)"]
  IC1 = 6n137 Optocoupler [package="DIP (Dual Inline) [THT]"]
  R6 = Resistor Mini [tolerance=±5% resistance=4.7k package=THT]
  R7 = Resistor [tolerance=±5% resistance=220 package="2512 [SMD]"]
  J9 = male pin header, 2 pins [form="♂ (male)"]
  J10 = male pin header, 3 pins [form="♂ (male)"]
  R9 = Resistor [tolerance=±5% resistance=220 package="2512 [SMD]"]
  R10 = Resistor [tolerance=±5% resistance=4.7k package="2512 [SMD]"]
  R11 = Resistor [tolerance=±5% resistance=4.7k package="2512 [SMD]"]
  R12 = Resistor Mini [tolerance=±5% resistance=220 package=THT]

nets:
  GND: RE1.GND, J2.pin2, RE2.GND, U1.NC1, C3.1, C5.-, Teensy1.GND#0, Teensy1.GND#55, J5.pin4, C7.-, C8.1, IC1.NC#3, IC1.GND, J10.pin2
  N1: J2.pin1, C3.0, C5.+, Teensy1.Vin, J5.pin3
  N2: J2.pin3, Teensy1.A9/D23, Teensy1.AREF
  N3: J2.pin4, Teensy1.A8/D22, Teensy1.A10
  N4: J2.pin5, Teensy1.D9
  N5: D1.cathode, U3.MIDI_IN, IC1.Vf-, J9.pin1
  N6: D1.anode, IC1.Vf+, R7.Pin_0
  N7: U3.MIDI_OUT, R7.Pin_1, J9.pin2
  N8: Teensy1.D0, IC1.Vo, R6.Pin_0
  N9: Teensy1.D2, J8.pin1
  N10: Teensy1.D3, J8.pin2
  N11: Teensy1.D4, J8.pin3
  N12: Teensy1.A4/D18, J5.pin2, R11.Pin_0
  N13: Teensy1.A5/D19, J5.pin1, R10.Pin_0
  N14: Teensy1.A7/D21, Teensy1.A11
  3V3: Teensy1.3V3, Teensy1.3V3_1, C7.+, C8.0, IC1.NC#0, IC1.Vcc, R6.Pin_1, R9.Pin_1, R10.Pin_1, R11.Pin_1
  N15: Teensy1.AGND, Teensy1.VUSB
  N16: Teensy1.D27, Teensy1.Vb
  N17: Teensy1.D28, J7.pin1
  N18: Teensy1.D29, J7.pin2
  N19: Teensy1.D30, J7.pin3
  N20: Teensy1.D38, Teensy1.R, Teensy1.P, Teensy1.GND#59
  N21: J10.pin1, R12.Pin_0
  N22: J10.pin3, R12.Pin_1

custom parts:
  KY-040 Rotary encoder: KY-040 Rotary Encoder with switch on breakout borad from AZ Delivery
  Teensy 3.6 (Basic): The Teensy is a complete USB-based microcontoller development system, in a very small footprint, capable of implementing many types of projects. All programming is done via the USB port. No special programmer is needed, only a standard micro-USB cable and a PC or Macintosh with a USB port.
  6n137 Optocoupler: 6n137 fast Optocoupler. With 8 pins on a 300mil dual inline package (DIP) footprint. Ve is strobe input. Output is inverting.
  Resistor Mini: A generic resistor (0.25W)
