# Fritzing sketch MicrodexedTouch (saved by Fritzing 0.9.9b)
stripboards: 1

parts:
  Teensy1 = Teensy 4.1
  RE1 = KY-040 Rotary encoder [package="Breakout board"]
  J2 = male pin header, 6 pins [form="♂ (male)"]
  RE2 = KY-040 Rotary encoder [package="Breakout board"]
  J3 = male pin header, 6 pins [form="♂ (male)"]
  U1 = MIDI_CONN_FEMALE_SUPPORT [package=din_5_female_support]
  U2 = LM 358 Dual Op-Amp [package="DIP8 [THT]"]
  R1 = Resistor [tolerance=±5% power=0.25 resistance=6.8k package=THT]
  D1 = Rectifier Diode [part_number=1N4001 package="300 mil [THT]"]
  R2 = Resistor [tolerance=±5% power=0.25 resistance=47 package=THT]
  R3 = Resistor [tolerance=±5% power=0.25 resistance=220 package=THT]
  C1 = Ceramic Capacitor [capacitance=100nF voltage=35V package="100 mil [THT, multilayer]"]
  C2 = Electrolytic Capacitor [capacitance=1µF voltage=35V package="100 mil [THT, electrolytic]"]
  C3 = Ceramic Capacitor [capacitance=100nF voltage=35V package="100 mil [THT, multilayer]"]
  C5 = Electrolytic Capacitor [capacitance=1µF voltage=35V package="100 mil [THT, electrolytic]"]
  C6 = Ceramic Capacitor [capacitance=100nF voltage=35V package="100 mil [THT, multilayer]"]
  J4 = male pin header, 8 pins [form="♂ (male)"]
  J5 = male pin header, 5 pins [form="♂ (male)"]
  U3 = MIDI_CONN_FEMALE_SUPPORT [package=din_5_female_support]
  R4 = Resistor [tolerance=±5% power=0.25 resistance=47 package=THT]

nets:
  GND: Teensy1.GND, Teensy1.GND2#55, RE1.GND, J2.pin2, RE2.GND, J3.pin4, U1.NC1, U2.connector0, U2.connector7, C1.0, C2.-, C3.1, C5.-, C6.1
  N1: Teensy1.D0, U2.connector1, U2.connector6, R1.Pin_1, D1.cathode, U3.MIDI_OUT
  N2: Teensy1.D1, R2.Pin_0
  N3: Teensy1.D2, Teensy1.A7/D21, J2.pin5
  N4: Teensy1.D5, Teensy1.A6/D20, J2.pin3
  N5: Teensy1.D6, J3.pin2
  N6: Teensy1.D7, J2.pin4
  N7: Teensy1.D9, Teensy1.D13, J3.pin5
  N8: Teensy1.D11, J3.pin6
  N9: Teensy1.D12, J3.pin3
  N10: Teensy1.3V3_LOW, J3.pin1, U2.connector3, U2.connector4, R1.Pin_0, C1.1, C5.+, C6.0, J4.pin8, R4.Pin_1
  N11: Teensy1.GND2#31, J4.pin2
  N12: Teensy1.A10/D24, J4.pin4
  N13: Teensy1.A11/D25, RE2.SW
  N14: Teensy1.A12/D26, J4.pin6, J5.pin3
  N15: Teensy1.A13/D27, Teensy1.D28, RE2.CLK
  N16: Teensy1.D29, RE2.DT
  N17: Teensy1.D30, RE1.SW
  N18: Teensy1.D31, RE1.DT
  N19: Teensy1.D32, RE1.CLK
  N20: Teensy1.D33, J5.pin5
  N21: Teensy1.D37, J4.pin5
  N22: Teensy1.A15/D39, J5.pin4
  N23: Teensy1.A17/D41, J4.pin3
  N24: J2.pin1, C2.+, C3.0, J4.pin1
  N25: U1.MIDI_IN, R4.Pin_0
  N26: U1.MIDI_OUT, R2.Pin_1
  N27: U2.connector2, U2.connector5, D1.anode, R3.Pin_1
  N28: R3.Pin_0, U3.MIDI_IN
  N29: J4.pin7, J5.pin1

custom parts:
  Teensy 4.1: The Teensy is a complete USB-based microcontoller development system, in a very small footprint, capable of implementing many types of projects. All programming is done via the USB port. No special programmer is needed, only a standard micro-USB cable and a PC or Macintosh with a USB port.
  KY-040 Rotary encoder: KY-040 Rotary Encoder with switch on breakout borad from AZ Delivery
