# Fritzing sketch minidexed2 (saved by Fritzing 0.9.9b)
stripboards: 2

parts:
  Pi_Header = Raspberry Pi Header 40pin [form="♂ (male)" package=THT]
  Encoder = Rotary Encoder with Knob
  IC1 = 6n137 Optocoupler [package="DIP (Dual Inline) [THT]"]
  D1 = Diode [package=diode-hv]
  R2 = Resistor [tolerance=±5% resistance=220 package="2512 [SMD]"]
  R3 = Resistor [tolerance=±5% resistance=4.7k package="2512 [SMD]"]
  C1 = Ceramic Capacitor [capacitance=100nF voltage=35V package="200 mil [THT, multilayer]"]
  Midi_DIN = female pin header, 2 pins [form="♀ (female)"]
  A1 = Raspberry Pi Pico H
  U1 = SWITCH_SPDT [package=kps-1290]
  C2 = Ceramic Capacitor [capacitance=10nF voltage=35V package="200 mil [THT, multilayer]"]
  C3 = Ceramic Capacitor [capacitance=10nF voltage=35V package="200 mil [THT, multilayer]"]
  R4 = Resistor [tolerance=±5% resistance=10k package="2512 [SMD]"]
  R5 = Resistor [tolerance=±5% resistance=10k package="2512 [SMD]"]
  R6 = Resistor [tolerance=±5% resistance=10k package="2512 [SMD]"]
  LC_1602_i2c = LCD1602-I2C
  RaspberryPi_USB_Midi_Keyboard_In = USB Connectors [package=usb-a-pcb]  # not connected

nets:
  3V3: Pi_Header.3v3, Pi_Header.3V3, IC1.NC#0, IC1.Vcc, R3.Pin_0, C1.0, R4.Pin_0, R5.Pin_0, R6.Pin_0, LC_1602_i2c.VCC
  N1: Pi_Header.GPIO2, LC_1602_i2c.SDA
  N2: Pi_Header.GPIO3, LC_1602_i2c.SCL
  GND: Pi_Header.GND, Encoder.no_name_yet#2, Encoder.no_name_yet#5, IC1.NC#3, IC1.GND, C1.1, A1.GND, C2.1, C3.1, LC_1602_i2c.GND
  N3: Pi_Header.GIPO10, Encoder.no_name_yet#1, C2.0, R5.Pin_1
  N4: Pi_Header.GIPO9, Encoder.no_name_yet#3, C3.0, R4.Pin_1
  N5: Pi_Header.GIPO11, Encoder.no_name_yet#4, R6.Pin_1
  N6: Pi_Header.GIPO15, U1.P
  N7: IC1.Vf+, D1.C, R2.Pin_1
  N8: IC1.Vf-, Midi_DIN.pin2
  N9: IC1.Vo, R3.Pin_1, U1.O
  N10: R2.Pin_0, Midi_DIN.pin1
  N11: A1.GP0, U1.S

notes:
  PCM5102A DAC
  6N137
  Pico RP20240

custom parts:
  Raspberry Pi Header 40pin: Raspberry Pi 40 pin header - for creating your own shields.
  Rotary Encoder with Knob: Rotary Encoder with 1/4" Shaft and Knob
  6n137 Optocoupler: 6n137 fast Optocoupler. With 8 pins on a 300mil dual inline package (DIP) footprint. Ve is strobe input. Output is inverting.
  Raspberry Pi Pico H: Raspberry Pi Pico H. Based around the RP2040 microcontroller the Pico H is a low cost microcontroller device bringing Raspberry Pi quality, cost, and easy of use to the microcontroller space.
  LCD1602-I2C: A standard character display, usually with 2x16 characters. Comes in many colors with LCM1602 IIC attached.
